// Logisim project FinalProject.circ as structural Verilog: 3 circuits, main circuit ALU_CIRC
module DATAPATH (
  input  [7:0] INP,
  input  [7:0] in_2
);

  wire button_1_out, button_2_out, button_3_out, clock_1_out, control_1_ac_write, control_1_mem_write,
       control_1_pc_skip, control_1_pc_source;
  wire [1:0] control_1_ac_source;
  wire [4:0] control_1_addr, register_1_q;
  wire [7:0] AC_q, alu_circ_1_result, INSTRUCTIONS_data, MEMORY_dout, multiplexer_2_out;

  Adder adder_1 (.a(in_2), .b(INSTRUCTIONS_data), .cin(control_1_pc_skip));  // open: out, cout
  CONTROL control_1 (
    .I(INSTRUCTIONS_data), .CUR_AC(AC_q), .ADDR(control_1_addr), .PC_SOURCE(control_1_pc_source),
    .PC_SKIP(control_1_pc_skip), .AC_SOURCE(control_1_ac_source), .MEM_WRITE(control_1_mem_write),
    .AC_WRITE(control_1_ac_write));  // open: ALU_SOURCE, PC_WRITE
  Multiplexer #(.width(5)) multiplexer_1 (.in0(control_1_addr), .sel(control_1_pc_source));  // open: in1, out
  Clock clock_1 (.out(clock_1_out));
  Button button_1 (.out(button_1_out));
  Multiplexer #(.select(2), .width(8)) multiplexer_2 (
    .in0(INP), .in1(MEMORY_dout), .in2(alu_circ_1_result), .out(multiplexer_2_out), .sel(control_1_ac_source));  // open: in3
  RAM #(.addrWidth(5), .clearpin("true"), .enables("line")) MEMORY (
    .addr(control_1_addr), .we(clock_1_out), .din(AC_q), .dout(MEMORY_dout), .clr(button_2_out));  // open: clk
  ROM #(.addrWidth(5)) INSTRUCTIONS (.addr(register_1_q), .data(INSTRUCTIONS_data));
  Register #(.width(5)) register_1 (.Q(register_1_q), .clk(clock_1_out), .clr(button_1_out));  // open: D, en
  Button button_2 (.out(button_2_out));
  ALU_CIRC alu_circ_1 (.a(AC_q), .b(MEMORY_dout), .Control(control_1_mem_write), .Result(alu_circ_1_result));
  Button button_3 (.out(button_3_out));
  Register AC (.D(multiplexer_2_out), .Q(AC_q), .clk(clock_1_out), .clr(button_3_out));  // open: en
endmodule

module ALU_CIRC (
  input  [7:0] a,
  input  [7:0] b,
  input  Control,
  output [7:0] Result
);

  wire [7:0] adder_1_out, subtractor_1_out;

  Adder adder_1 (.a(a), .b(b), .out(adder_1_out));  // open: cin, cout
  Subtractor subtractor_1 (.a(a), .b(b), .out(subtractor_1_out));  // open: bin, bout
  Multiplexer #(.width(8)) multiplexer_1 (.in0(adder_1_out), .in1(subtractor_1_out), .out(Result), .sel(Control));
endmodule

module CONTROL (
  input  [7:0] I,
  input  [7:0] CUR_AC,
  output [4:0] ADDR,
  output PC_SOURCE,
  output PC_SKIP,
  output [1:0] AC_SOURCE,
  output ALU_SOURCE,
  output MEM_WRITE,
  output PC_WRITE,
  output AC_WRITE
);

  wire comparator_1_gt, comparator_1_lt, multiplexer_1_out;
  wire [6:6] multiplexer_2_out;

  Comparator comparator_1 (.a({8{1'b0}}), .b(CUR_AC), .gt(comparator_1_gt), .lt(comparator_1_lt));  // open: eq
  Multiplexer #(.select(2)) multiplexer_1 (
    .in1(comparator_1_gt), .in3(comparator_1_lt), .out(multiplexer_1_out), .sel(I[4:3]));  // open: in0, in2
  Multiplexer #(.select(3), .width(8)) multiplexer_2 (
    .in0({8{1'b0}}), .in1({8{1'b0}}), .in2({8{1'b0}}), .in3({8{1'b0}}), .in4({8{1'b0}}), .in5({8{1'b0}}),
    .in6({8{1'b0}}), .in7({8{1'b0}}),
    .out({PC_SOURCE, multiplexer_2_out[6], AC_SOURCE, ALU_SOURCE, MEM_WRITE, {2{AC_WRITE}}}), .sel(I[7:5]));
  and and_1 (PC_SKIP, PC_SOURCE, multiplexer_2_out[6], AC_WRITE, multiplexer_1_out);

  assign ADDR = I[4:0];
  assign PC_WRITE = AC_WRITE;
endmodule
